// Logisim project arquitetura_de_computadores_14_03_2024.circ as structural Verilog: 12 circuits, main circuit main
module main (
  input  D,
  input  [3:0] A,
  input  [3:0] B,
  input  [2:0] in_4,
  input  [3:0] A_2,
  input  [3:0] B_2,
  input  D_2,
  input  [2:0] \Operação ,
  output out_9,
  output out_10,
  output [3:0] out_11,
  output out_12,
  output out_13,
  output [3:0] S
);

  wire decoder_3x8_1_s0, decoder_3x8_1_s1, decoder_3x8_1_s2, decoder_3x8_1_s3, decoder_3x8_1_s4,
       decoder_3x8_1_s5, not_1_out;
  wire [3:0] ad_4_1_out_5, buffer_5_s, or_1_s, rot_l_1_abcd_2, rot_w_1_abcd_2, sub_4_1_out_5;

  DECODER_3x8 decoder_3x8_1 (
    .S0(decoder_3x8_1_s0), .S1(decoder_3x8_1_s1), .S2(decoder_3x8_1_s2), .S3(decoder_3x8_1_s3),
    .S4(decoder_3x8_1_s4), .S5(decoder_3x8_1_s5), .in_1(in_4));  // open: S6, S7
  BUFFER buffer_1 (.in_2(decoder_3x8_1_s0), .B(B), .S(out_11));
  ULA ula_1 (.D(D_2), .A(A_2), .B(B_2), .out_5(out_12), .out_6(out_13), .in_4(\Operação ), .out_7(S));
  AD_4 ad_4_1 (.in_2(A), .out_4(out_9), .in_1(B), .in_3(1'b0), .out_5(ad_4_1_out_5));
  BUFFER buffer_2 (.in_2(decoder_3x8_1_s1), .B(ad_4_1_out_5), .S(out_11));
  SUB_4 sub_4_1 (.in_2(A), .out_4(out_10), .in_1(B), .in_3(1'b0), .out_5(sub_4_1_out_5));
  BUFFER buffer_3 (.in_2(decoder_3x8_1_s2), .B(sub_4_1_out_5), .S(out_11));
  OR or_1 (.A(A), .B(B), .S(or_1_s));
  BUFFER buffer_4 (.in_2(decoder_3x8_1_s3), .B(or_1_s), .S(out_11));
  BUFFER_CONTROLADO_INVERTIDO buffer_controlado_invertido_1 (.in_2(decoder_3x8_1_s4), .S(out_11), .B(B));
  ROT_W rot_w_1 (.abcd_2(rot_w_1_abcd_2), .ABCD(A), .XY(B[1:0]));
  ROT_L rot_l_1 (.abcd_2(rot_l_1_abcd_2), .ABCD(A), .XY(B[1:0]));
  not not_1 (not_1_out, D);
  BUFFER buffer_5 (.in_2(D), .B(rot_w_1_abcd_2), .S(buffer_5_s));
  BUFFER buffer_6 (.in_2(not_1_out), .B(rot_l_1_abcd_2), .S(buffer_5_s));
  BUFFER buffer_7 (.in_2(decoder_3x8_1_s5), .B(buffer_5_s), .S(out_11));
endmodule

module AD_1 (
  input  A,
  input  B,
  input  Vem_1,
  output S,
  output Vai_1
);

  wire and_1_out, and_2_out, or_1_out, xor_1_out;

  xor xor_1 (xor_1_out, A, B);
  or or_1 (or_1_out, Vem_1, B);
  and and_1 (and_1_out, Vem_1, B);
  xor xor_2 (S, xor_1_out, Vem_1);
  and and_2 (and_2_out, or_1_out, A);
  or or_2 (Vai_1, and_2_out, and_1_out);
endmodule

module AD_4 (
  input  [3:0] in_1,
  input  [3:0] in_2,
  input  in_3,
  output out_4,
  output [3:0] out_5
);

  wire ad_1_2_vai_1, ad_1_3_vai_1, ad_1_4_vai_1;

  AD_1 ad_1_1 (.A(in_2[3]), .B(in_1[3]), .S(out_5[3]), .Vem_1(ad_1_2_vai_1), .Vai_1(out_4));
  AD_1 ad_1_2 (.A(in_2[2]), .B(in_1[2]), .S(out_5[2]), .Vem_1(ad_1_4_vai_1), .Vai_1(ad_1_2_vai_1));
  AD_1 ad_1_3 (.A(in_2[0]), .B(in_1[0]), .S(out_5[0]), .Vem_1(in_3), .Vai_1(ad_1_3_vai_1));
  AD_1 ad_1_4 (.A(in_2[1]), .B(in_1[1]), .S(out_5[1]), .Vem_1(ad_1_3_vai_1), .Vai_1(ad_1_4_vai_1));
endmodule

module SUB_1 (
  input  A,
  input  B,
  input  Vem_1,
  output S,
  output Vai_1
);

  wire and_1_out, and_2_out, not_1_out, or_1_out, xor_1_out;

  not not_1 (not_1_out, A);
  xor xor_1 (xor_1_out, A, B);
  or or_1 (or_1_out, Vem_1, B);
  and and_1 (and_1_out, Vem_1, B);
  xor xor_2 (S, xor_1_out, Vem_1);
  and and_2 (and_2_out, or_1_out, not_1_out);
  or or_2 (Vai_1, and_2_out, and_1_out);
endmodule

module SUB_4 (
  input  [3:0] in_1,
  input  [3:0] in_2,
  input  in_3,
  output out_4,
  output [3:0] out_5
);

  wire sub_1_2_vai_1, sub_1_3_vai_1, sub_1_4_vai_1;

  SUB_1 sub_1_1 (.A(in_2[3]), .B(in_1[3]), .Vem_1(sub_1_2_vai_1), .S(out_5[3]), .Vai_1(out_4));
  SUB_1 sub_1_2 (.A(in_2[2]), .B(in_1[2]), .Vem_1(sub_1_4_vai_1), .S(out_5[2]), .Vai_1(sub_1_2_vai_1));
  SUB_1 sub_1_3 (.A(in_2[0]), .B(in_1[0]), .Vem_1(in_3), .S(out_5[0]), .Vai_1(sub_1_3_vai_1));
  SUB_1 sub_1_4 (.A(in_2[1]), .B(in_1[1]), .Vem_1(sub_1_3_vai_1), .S(out_5[1]), .Vai_1(sub_1_4_vai_1));
endmodule

module BUFFER (
  input  [3:0] B,
  input  in_2,
  output [3:0] S
);

  assign S[2] = in_2 ? B[2] : 1'bz;  // Controlled_Buffer controlled_buffer_1
  assign S[3] = in_2 ? B[3] : 1'bz;  // Controlled_Buffer controlled_buffer_2
  assign S[0] = in_2 ? B[0] : 1'bz;  // Controlled_Buffer controlled_buffer_3
  assign S[1] = in_2 ? B[1] : 1'bz;  // Controlled_Buffer controlled_buffer_4
endmodule

module BUFFER_CONTROLADO_INVERTIDO (
  input  [3:0] B,
  input  in_2,
  output [3:0] S
);

  assign S[3] = in_2 ? ~B[3] : 1'bz;  // Controlled_Inverter controlled_inverter_1
  assign S[2] = in_2 ? ~B[2] : 1'bz;  // Controlled_Inverter controlled_inverter_2
  assign S[1] = in_2 ? ~B[1] : 1'bz;  // Controlled_Inverter controlled_inverter_3
  assign S[0] = in_2 ? ~B[0] : 1'bz;  // Controlled_Inverter controlled_inverter_4
endmodule

module DECODER_3x8 (
  input  [2:0] in_1,
  output S0,
  output S1,
  output S2,
  output S3,
  output S4,
  output S5,
  output S6,
  output S7
);

  wire not_1_out, not_2_out, not_3_out, not_4_out, not_5_out, not_6_out, not_7_out, not_8_out, not_9_out,
       not_10_out, not_11_out, not_12_out;

  not not_1 (not_1_out, in_1[2]);
  not not_2 (not_2_out, in_1[1]);
  not not_3 (not_3_out, in_1[0]);
  not not_4 (not_4_out, in_1[2]);
  not not_5 (not_5_out, in_1[1]);
  not not_6 (not_6_out, in_1[2]);
  not not_7 (not_7_out, in_1[0]);
  not not_8 (not_8_out, in_1[2]);
  not not_9 (not_9_out, in_1[1]);
  not not_10 (not_10_out, in_1[0]);
  not not_11 (not_11_out, in_1[1]);
  not not_12 (not_12_out, in_1[0]);
  and and_1 (S7, in_1[2], in_1[1], in_1[0]);
  and and_2 (S0, not_1_out, not_2_out, not_3_out);
  and and_3 (S1, not_4_out, not_5_out, in_1[0]);
  and and_4 (S2, not_6_out, in_1[1], not_7_out);
  and and_5 (S3, not_8_out, in_1[1], in_1[0]);
  and and_6 (S4, in_1[2], not_9_out, not_10_out);
  and and_7 (S5, in_1[2], not_11_out, in_1[0]);
  and and_8 (S6, in_1[2], in_1[1], not_12_out);
endmodule

module ROT_L (
  input  [3:0] ABCD,
  input  [1:0] XY,
  output [3:0] abcd_2
);

  wire and_1_out, and_2_out, and_3_out, and_4_out, and_5_out, and_6_out, and_7_out, and_8_out, and_9_out;

  and and_1 (and_1_out, ~XY[1], ~XY[0], ABCD[3]);  // AND_Gate
  and and_2 (and_2_out, ~XY[1], XY[0], ABCD[2]);  // AND_Gate
  and and_3 (and_3_out, XY[1], ~XY[0], ABCD[1]);  // AND_Gate
  and and_4 (and_4_out, XY[1], XY[0], ABCD[0]);
  and and_5 (and_5_out, ~XY[1], ~XY[0], ABCD[2]);  // AND_Gate
  and and_6 (and_6_out, ~XY[1], XY[0], ABCD[1]);  // AND_Gate
  and and_7 (and_7_out, XY[1], ~XY[0], ABCD[0]);  // AND_Gate
  and and_8 (and_8_out, ~XY[1], ~XY[0], ABCD[1]);  // AND_Gate
  and and_9 (and_9_out, ~XY[1], XY[0], ABCD[0]);  // AND_Gate
  and and_10 (abcd_2[0], ~XY[1], ~XY[0], ABCD[0]);  // AND_Gate
  or or_1 (abcd_2[3], and_1_out, and_2_out, and_3_out, and_4_out);
  or or_2 (abcd_2[2], and_5_out, and_6_out, and_7_out);
  or or_3 (abcd_2[1], and_8_out, and_9_out);
endmodule

module ROT_W (
  input  [3:0] ABCD,
  input  [1:0] XY,
  output [3:0] abcd_2
);

  wire and_1_out, and_2_out, and_3_out, and_4_out, and_5_out, and_6_out, and_7_out, and_8_out, and_9_out;

  and and_1 (and_1_out, ~XY[1], ~XY[0], ABCD[0]);  // AND_Gate
  and and_2 (and_2_out, ~XY[1], XY[0], ABCD[1]);  // AND_Gate
  and and_3 (and_3_out, XY[1], ~XY[0], ABCD[2]);  // AND_Gate
  and and_4 (and_4_out, XY[1], XY[0], ABCD[3]);
  and and_5 (and_5_out, ~XY[1], ~XY[0], ABCD[1]);  // AND_Gate
  and and_6 (and_6_out, ~XY[1], XY[0], ABCD[2]);  // AND_Gate
  and and_7 (and_7_out, XY[1], ~XY[0], ABCD[3]);  // AND_Gate
  and and_8 (and_8_out, ~XY[1], ~XY[0], ABCD[2]);  // AND_Gate
  and and_9 (and_9_out, ~XY[1], XY[0], ABCD[3]);  // AND_Gate
  and and_10 (abcd_2[3], ~XY[1], ~XY[0], ABCD[3]);  // AND_Gate
  or or_1 (abcd_2[0], and_1_out, and_2_out, and_3_out, and_4_out);
  or or_2 (abcd_2[1], and_5_out, and_6_out, and_7_out);
  or or_3 (abcd_2[2], and_8_out, and_9_out);
endmodule

module OR (
  input  [3:0] A,
  input  [3:0] B,
  output [3:0] S
);

  or or_1 (S[2], A[2], B[2]);
  or or_2 (S[3], A[3], B[3]);
  or or_3 (S[1], A[1], B[1]);
  or or_4 (S[0], A[0], B[0]);
endmodule

module ULA (
  input  D,
  input  [3:0] A,
  input  [3:0] B,
  input  [2:0] in_4,
  output out_5,
  output out_6,
  output [3:0] out_7
);

  wire decoder_3x8_1_s0, decoder_3x8_1_s1, decoder_3x8_1_s2, decoder_3x8_1_s3, decoder_3x8_1_s4,
       decoder_3x8_1_s5, not_1_out;
  wire [3:0] ad_4_1_out_5, buffer_5_s, or_1_s, rot_l_1_abcd_2, rot_w_1_abcd_2, sub_4_1_out_5;

  DECODER_3x8 decoder_3x8_1 (
    .S0(decoder_3x8_1_s0), .S1(decoder_3x8_1_s1), .S2(decoder_3x8_1_s2), .S3(decoder_3x8_1_s3),
    .S4(decoder_3x8_1_s4), .S5(decoder_3x8_1_s5), .in_1(in_4));  // open: S6, S7
  BUFFER buffer_1 (.in_2(decoder_3x8_1_s0), .B(B), .S(out_7));
  AD_4 ad_4_1 (.in_2(A), .out_4(out_5), .in_1(B), .in_3(1'b0), .out_5(ad_4_1_out_5));
  BUFFER buffer_2 (.in_2(decoder_3x8_1_s1), .B(ad_4_1_out_5), .S(out_7));
  SUB_4 sub_4_1 (.in_2(A), .out_4(out_6), .in_1(B), .in_3(1'b0), .out_5(sub_4_1_out_5));
  BUFFER buffer_3 (.in_2(decoder_3x8_1_s2), .B(sub_4_1_out_5), .S(out_7));
  OR or_1 (.A(A), .B(B), .S(or_1_s));
  BUFFER buffer_4 (.in_2(decoder_3x8_1_s3), .B(or_1_s), .S(out_7));
  BUFFER_CONTROLADO_INVERTIDO buffer_controlado_invertido_1 (.in_2(decoder_3x8_1_s4), .S(out_7), .B(B));
  ROT_W rot_w_1 (.abcd_2(rot_w_1_abcd_2), .ABCD(A), .XY(B[1:0]));
  ROT_L rot_l_1 (.abcd_2(rot_l_1_abcd_2), .ABCD(A), .XY(B[1:0]));
  not not_1 (not_1_out, D);
  BUFFER buffer_5 (.in_2(D), .B(rot_w_1_abcd_2), .S(buffer_5_s));
  BUFFER buffer_6 (.in_2(not_1_out), .B(rot_l_1_abcd_2), .S(buffer_5_s));
  BUFFER buffer_7 (.in_2(decoder_3x8_1_s5), .B(buffer_5_s), .S(out_7));
endmodule
